# Fritzing sketch Schematic (saved by Fritzing 0.9.3b)
breadboards: 1

parts:
  Part2 = Arduino Mega 2560 (Rev3)
  S1 = H-Bridge with L298N
  Right_Motor = Stepper Motor - Unipolar
  Left_Motor = Stepper Motor - Unipolar
  LIPO_2S_Battery = LiPoly Battery (1300mAh)
  Switch = Toggle Switch [package=THT]

nets:
  N1: Part2.D12_PWM, Right_Motor.D
  N2: Part2.D11_PWM, Left_Motor.D
  N3: Part2.D10_PWM, S1.ENB
  N4: Part2.D9_PWM, S1.ENA
  N5: Part2.5V, Right_Motor.A, Left_Motor.A
  GND: Part2.GND, S1.GND, Right_Motor.COMMON_1, Left_Motor.COMMON_1, LIPO_2S_Battery.negative
  VIN: Part2.VIN, S1.5V
  N6: Part2.D2_PWM, Left_Motor.COMMON_2
  N7: Part2.D3_PWM, Right_Motor.COMMON_2
  N8: Part2.D4_PWM, S1.IN3
  N9: Part2.D5_PWM, S1.IN4
  N10: Part2.D6_PWM, S1.IN1
  N11: Part2.D7_PWM, S1.IN2
  N12: S1.12V, Switch.COM
  N13: S1.M1-01, Left_Motor.B
  N14: S1.M1-02, Left_Motor.C
  N15: S1.M2-01, Right_Motor.B
  N16: S1.M2-02, Right_Motor.C
  N17: LIPO_2S_Battery.positive, Switch.L2

custom parts:
  H-Bridge with L298N: h-bridge
  LiPoly Battery (1300mAh): Lithium Ion Polymer Battery (1300mAh)
